# Fritzing sketch research project - setup 1 schema (saved by Fritzing 0.9.3b)

parts:
  Part1 = Arduino Leonardo (Rev3b)
  U1 = NodeMCU V1.0
  Part2 = MicroSD Card Module
  Part3 = ACS712 Low Current Sensor Board v12
  ENC28J1 = ENC28J60
  Q1 = NPN-Transistor [package="TO92 [THT]"]
  R1 = Resistor [tolerance=±5% resistance=220 package="0402 [SMD]"]
  DHT1 = DHT22 Humidity and Temperature Sensor

nets:
  N1: Part1.D4/A6, Part2.CS
  N2: Part1.D5_PWM, U1.RX
  N3: Part1.D6_PWM/A7, U1.TX
  N4: Part1.D7, DHT1.DATA
  N5: Part1.3V3, Part3.IP-
  5V: Part1.5V, Part2.VCC, Part3.5V, DHT1.VDD
  GND: Part1.GND, Part1.A0, U1.GND, Part2.GND, Part3.VO, Part3.GND, ENC28J1.GND, DHT1.NULL, DHT1.GND
  N6: Part1.D11_PWM, Part2.MOSI
  N7: Part1.D12/A11, Part2.MISO
  N8: Part1.D13_PWM, Part2.SCK
  N9: U1.D1, U1.D7, ENC28J1.INT, ENC28J1.SO
  N10: U1.D2, ENC28J1.SCK, ENC28J1.RST
  N11: U1.D5, ENC28J1.CLK
  N12: U1.D6, ENC28J1.SI
  N13: U1.D8, Q1.C
  N14: U1.3V3, Part3.IP+, ENC28J1.3.3
  N15: ENC28J1.CS, R1.Pin_1
  N16: Q1.B, R1.Pin_0

custom parts:
  NodeMCU V1.0: ESP8266 based NodeMCU
  ENC28J60: Ethernet Module ENC28J60
