# Fritzing sketch research project - setup 2 schema (saved by Fritzing 0.9.3b)

parts:
  Part1 = Arduino Leonardo (Rev3b)
  Part3 = ACS712 Low Current Sensor Board v12
  DHT1 = DHT22 Humidity and Temperature Sensor
  Part4 = Arduino Ethernet Shield (Rev3)
  VCC1 = Battery block 9V  # not connected
  U2 = Unproven! [package=msop-10]

nets:
  GND: Part1.GND, DHT1.NULL, DHT1.GND
  N1: Part3.IP+, U2.Power
  5V: Part3.5V, Part4.5V
  GND_2: Part3.VO, Part3.GND, Part4.A0, Part4.GND
  VDD: DHT1.VDD, Part4.3V3
  N2: DHT1.DATA, Part4.D7

custom parts:
  Unproven!: Stand-alone Linear Li-ion/Li-polymer Charge Management Controller Packages: DFN-10, MSOP-10 Last modified: 8/17/10 Unproven!
